// Logisim project realALU.circ as structural Verilog
module AND (
  input  [7:0] inA,
  input  [7:0] inB,
  output [7:0] out
);

  assign out = inA & inB;  // AND_Gate and_1, 8 bits wide
endmodule
